# Fritzing sketch CircuitSketch (saved by Fritzing 0.8.7b)
breadboards: 1

parts:
  Play = SWITCH-MOMENTARY-2 [package=tactile-pth-12mm]
  Unpause = SWITCH-MOMENTARY-2 [package=tactile-pth-12mm]
  Stop = SWITCH-MOMENTARY-2 [package=tactile-pth-12mm]
  Pause = SWITCH-MOMENTARY-2 [package=tactile-pth-12mm]
  Next = SWITCH-MOMENTARY-2 [package=tactile-pth-12mm]
  R1 = Resistor [tolerance=±5% resistance=1M package=THT]  # not connected
  R2 = Resistor [tolerance=±5% resistance=1M package=THT]  # not connected
  R3 = Resistor [tolerance=±5% resistance=1M package=THT]  # not connected
  R4 = Resistor [tolerance=±5% resistance=1M package=THT]  # not connected
  R6 = Resistor [tolerance=±5% resistance=1M package=THT]  # not connected
  R7 = Resistor [tolerance=±5% resistance=1M package=THT]  # not connected
  LED1 = LED - 5mm [color="Red (633nm)" package="5 mm [THT]"]
  LED2 = LED - 5mm [color="Red (633nm)" package="5 mm [THT]"]
  Prev = SWITCH-MOMENTARY-2 [package=tactile-pth-12mm]
  Raspberry_Pi_1 = Raspberry Pi 3
  R8 = Resistor [tolerance=±5% resistance=100 package=THT]
  R9 = Resistor [tolerance=±5% resistance=100 package=THT]
  R10 = Resistor [tolerance=±5% resistance=1M package=THT]
  R11 = Resistor [tolerance=±5% resistance=220 package=THT]
  R12 = Resistor [tolerance=±5% resistance=220 package=THT]  # not connected
  R13 = Resistor [tolerance=±5% resistance=1M package=THT]  # not connected
  R14 = Resistor [tolerance=±5% resistance=1M package=THT]  # not connected
  R15 = Resistor [tolerance=±5% resistance=1M package=THT]  # not connected

nets:
  N1: Play.1, Raspberry_Pi_1.GIPO24
  N2: Unpause.2, Raspberry_Pi_1.GIPO19
  N3: Stop.1, Raspberry_Pi_1.GIPO16
  N4: Pause.2, Raspberry_Pi_1.GIPO13
  N5: Next.1, Raspberry_Pi_1.GIPO25
  GND: LED1.cathode, LED2.cathode, Raspberry_Pi_1.GIPO21, R8.Pin_1, R9.Pin_1
  N6: Prev.1, Raspberry_Pi_1.GIPO23
  3V3: Raspberry_Pi_1.3v3, Raspberry_Pi_1.3V3
  N7: Raspberry_Pi_1.GIPO12, R10.Pin_0
  N8: Raspberry_Pi_1.5V, R11.Pin_0

notes:
  drill
